// Logisim project cpu.circ as structural Verilog: 5 circuits, main circuit main
module main (
);

  wire and_1_out, button_1_out, clock_1_out, instruction_spliter_1_add_r2r, instruction_spliter_1_add_r2v,
       instruction_spliter_1_cmp_r2r, instruction_spliter_1_cmp_r2v, instruction_spliter_1_jeq,
       instruction_spliter_1_jgt, instruction_spliter_1_jlt, instruction_spliter_1_ld_r2m,
       instruction_spliter_1_ld_r2r, instruction_spliter_1_ld_r2v, instruction_spliter_1_noop,
       instruction_spliter_1_st_r2m, instruction_spliter_1_st_r2r, instruction_spliter_1_sth_r2r,
       instruction_spliter_1_sth_r2v, instruction_spliter_1_stl_r2m, instruction_spliter_1_stl_r2r,
       instruction_spliter_1_sub_r2r, instruction_spliter_1_sub_r2v, not_1_out;
  wire [7:0] instruction_spliter_1_p1, instruction_spliter_1_p2_l, instruction_spliter_1_p2_u, register_2_q,
       undriven;
  wire [15:0] counter_1_q, instruction_spliter_1_p2, register_1_q;
  wire [39:0] rom_1_data;

  ROM #(.addrWidth(16), .dataWidth(40)) rom_1 (.addr(counter_1_q), .data(rom_1_data));
  Clock clock_1 (.out(clock_1_out));
  Button button_1 (.out(button_1_out));
  not not_1 (not_1_out, register_2_q[7]);
  and and_1 (and_1_out, clock_1_out, not_1_out);
  Counter #(.max('hffff), .trigger("falling"), .width(16)) counter_1 (
    .clr(button_1_out), .load(register_2_q[6]), .up(1'b1), .count(not_1_out), .clk(and_1_out),
    .D(register_1_q), .Q(counter_1_q));  // open: carry
  // Probe on instruction_spliter_1_p2
  // Probe on instruction_spliter_1_p2_l
  Instruction_Spliter instruction_spliter_1 (
    .Instruction(rom_1_data), .Enable(not_1_out), .P2(instruction_spliter_1_p2),
    .P2_L(instruction_spliter_1_p2_l), .P2_U(instruction_spliter_1_p2_u), .P1(instruction_spliter_1_p1),
    .HALT(undriven[7]), .NOOP(instruction_spliter_1_noop), .SUB_R2R(instruction_spliter_1_sub_r2r),
    .ADD_R2R(instruction_spliter_1_add_r2r), .SUB_R2V(instruction_spliter_1_sub_r2v),
    .ADD_R2V(instruction_spliter_1_add_r2v), .JMP(undriven[6]), .JLT(instruction_spliter_1_jlt),
    .JGT(instruction_spliter_1_jgt), .JEQ(instruction_spliter_1_jeq),
    .CMP_R2V(instruction_spliter_1_cmp_r2v), .CMP_R2R(instruction_spliter_1_cmp_r2r),
    .STH_R2R(instruction_spliter_1_sth_r2r), .STL_R2R(instruction_spliter_1_stl_r2r),
    .ST_R2R(instruction_spliter_1_st_r2r), .STH_R2V(instruction_spliter_1_sth_r2v),
    .STL_R2M(instruction_spliter_1_stl_r2m), .ST_R2M(instruction_spliter_1_st_r2m),
    .LD_R2M(instruction_spliter_1_ld_r2m), .LD_R2R(instruction_spliter_1_ld_r2r),
    .LD_R2V(instruction_spliter_1_ld_r2v));
  Register #(.trigger("falling"), .width(16)) register_1 (
    .D(instruction_spliter_1_p2), .en(register_2_q[6]), .clk(and_1_out), .Q(register_1_q), .clr(button_1_out));
  // Probe on instruction_spliter_1_p2_u
  // Probe on instruction_spliter_1_p1
  Register register_2 (.D(undriven), .en(and_1_out), .clk(and_1_out), .Q(register_2_q), .clr(button_1_out));
  RegisterFile registerfile_1 ();  // open: Clock, Reset, Data, Read_Addr, Write_Addr, Out_Data

  // Notes on the sheet:
  //   contents of rom_1 (hex, n*v repeats v):
  //   33000001 10041 20065 42010002 fffeffffff
endmodule

module Instruction_Spliter (
  input  [39:0] Instruction,
  input  Enable,
  output [15:0] P2,
  output [7:0] P2_L,
  output [7:0] P2_U,
  output [7:0] P1,
  output HALT,
  output NOOP,
  output SUB_R2R,
  output ADD_R2R,
  output SUB_R2V,
  output ADD_R2V,
  output JMP,
  output JLT,
  output JGT,
  output JEQ,
  output CMP_R2V,
  output CMP_R2R,
  output STH_R2R,
  output STL_R2R,
  output ST_R2R,
  output STH_R2V,
  output STL_R2M,
  output ST_R2M,
  output LD_R2M,
  output LD_R2R,
  output LD_R2V
);

  // Probe on Instruction[39:24]
  Instruction_Decoder instruction_decoder_1 (
    .Data(Instruction[39:24]), .Enable(Enable), .HALT(HALT), .NOOP(NOOP), .SUB_R2R(SUB_R2R),
    .ADD_R2R(ADD_R2R), .SUB_R2V(SUB_R2V), .ADD_R2V(ADD_R2V), .JMP(JMP), .JLT(JLT), .JGT(JGT), .JEQ(JEQ),
    .CMP_R2V(CMP_R2V), .CMP_R2R(CMP_R2R), .STH_R2R(STH_R2R), .STL_R2R(STL_R2R), .ST_R2R(ST_R2R),
    .STH_R2V(STH_R2V), .STL_R2M(STL_R2M), .ST_R2M(ST_R2M), .LD_R2M(LD_R2M), .LD_R2R(LD_R2R), .LD_R2V(LD_R2V));

  assign P1 = Instruction[23:16];
  assign P2 = Instruction[15:0];
  assign P2_L = Instruction[7:0];
  assign P2_U = Instruction[15:8];
endmodule

module Instruction_Decoder (
  input  [15:0] Data,
  input  Enable,
  output HALT,
  output NOOP,
  output SUB_R2R,
  output ADD_R2R,
  output SUB_R2V,
  output ADD_R2V,
  output JMP,
  output JLT,
  output JGT,
  output JEQ,
  output CMP_R2V,
  output CMP_R2R,
  output STH_R2R,
  output STL_R2R,
  output ST_R2R,
  output STH_R2V,
  output STL_R2M,
  output ST_R2M,
  output LD_R2M,
  output LD_R2R,
  output LD_R2V
);

  wire and_1_out, and_2_out, and_3_out, and_4_out, and_5_out, and_6_out, and_7_out, and_8_out, and_9_out,
       and_10_out, and_11_out, and_12_out, and_13_out, and_14_out, and_15_out, and_16_out, and_17_out,
       and_18_out, and_19_out, and_20_out, and_21_out, not_1_out, not_2_out, not_3_out, not_4_out, not_5_out,
       not_6_out, not_7_out, not_8_out, not_9_out, not_10_out, not_11_out, not_12_out, not_13_out,
       not_14_out, not_15_out, not_16_out, not_17_out, not_18_out, not_19_out, not_20_out, not_21_out,
       not_22_out, not_23_out, not_24_out, not_25_out, not_26_out, not_27_out, not_28_out, not_29_out,
       not_30_out, not_31_out, not_32_out, not_33_out, not_34_out, not_35_out, not_36_out, not_37_out,
       not_38_out, not_39_out, not_40_out, not_41_out, not_42_out, not_43_out, not_44_out, not_45_out,
       not_46_out, not_47_out, not_48_out, not_49_out, not_50_out, not_51_out, not_52_out, not_53_out,
       not_54_out, not_55_out, not_56_out, not_57_out, not_58_out, not_59_out, not_60_out, not_61_out,
       not_62_out, not_63_out, not_64_out, not_65_out, not_66_out, not_67_out, not_68_out, not_69_out,
       not_70_out, not_71_out, not_72_out, not_73_out, not_74_out, not_75_out, not_76_out, not_77_out,
       not_78_out, not_79_out, not_80_out, not_81_out, not_82_out, not_83_out, not_84_out, not_85_out,
       not_86_out, not_87_out, not_88_out, not_89_out, not_90_out, not_91_out, not_92_out, not_93_out,
       not_94_out, not_95_out, not_96_out, not_97_out, not_98_out, not_99_out, not_100_out, not_101_out,
       not_102_out, not_103_out, not_104_out, not_105_out, not_106_out, not_107_out, not_108_out,
       not_109_out, not_110_out, not_111_out, not_112_out, not_113_out, not_114_out, not_115_out,
       not_116_out, not_117_out, not_118_out, not_119_out, not_120_out, not_121_out, not_122_out,
       not_123_out, not_124_out, not_125_out, not_126_out, not_127_out, not_128_out, not_129_out,
       not_130_out, not_131_out, not_132_out, not_133_out, not_134_out, not_135_out, not_136_out,
       not_137_out, not_138_out, not_139_out, not_140_out, not_141_out, not_142_out, not_143_out,
       not_144_out, not_145_out, not_146_out, not_147_out, not_148_out, not_149_out, not_150_out,
       not_151_out, not_152_out, not_153_out, not_154_out, not_155_out, not_156_out, not_157_out,
       not_158_out, not_159_out, not_160_out, not_161_out, not_162_out, not_163_out, not_164_out,
       not_165_out, not_166_out, not_167_out, not_168_out, not_169_out, not_170_out, not_171_out,
       not_172_out, not_173_out, not_174_out, not_175_out, not_176_out, not_177_out, not_178_out,
       not_179_out, not_180_out, not_181_out, not_182_out, not_183_out, not_184_out, not_185_out,
       not_186_out, not_187_out, not_188_out, not_189_out, not_190_out, not_191_out, not_192_out,
       not_193_out, not_194_out, not_195_out, not_196_out, not_197_out, not_198_out, not_199_out,
       not_200_out, not_201_out, not_202_out, not_203_out, not_204_out, not_205_out, not_206_out,
       not_207_out, not_208_out, not_209_out, not_210_out, not_211_out, not_212_out, not_213_out,
       not_214_out, not_215_out, not_216_out, not_217_out, not_218_out, not_219_out, not_220_out,
       not_221_out, not_222_out, not_223_out, not_224_out, not_225_out, not_226_out, not_227_out,
       not_228_out, not_229_out, not_230_out, not_231_out, not_232_out, not_233_out, not_234_out,
       not_235_out, not_236_out, not_237_out, not_238_out, not_239_out, not_240_out, not_241_out,
       not_242_out, not_243_out, not_244_out, not_245_out, not_246_out, not_247_out, not_248_out,
       not_249_out, not_250_out, not_251_out, not_252_out, not_253_out, not_254_out, not_255_out,
       not_256_out, not_257_out, not_258_out, not_259_out, not_260_out, not_261_out, not_262_out,
       not_263_out, not_264_out, not_265_out, not_266_out, not_267_out;

  // Probe on Data
  // Probe on Data[15:12]
  // Probe on Data[11:8]
  // Probe on Data[7:4]
  // Probe on Data[3:0]
  not not_1 (not_1_out, Data[0]);
  and and_1 (and_1_out, not_1_out, Data[1], Data[2], Data[3], Data[4], Data[5], Data[6], Data[7], Data[8], Data[9], Data[10], Data[11], Data[12], Data[13], Data[14], Data[15]);
  and and_2 (and_2_out, Data[0], Data[1], Data[2], Data[3], Data[4], Data[5], Data[6], Data[7], Data[8], Data[9], Data[10], Data[11], Data[12], Data[13], Data[14], Data[15]);
  not not_2 (not_2_out, Data[2]);
  not not_3 (not_3_out, Data[3]);
  not not_4 (not_4_out, Data[4]);
  not not_5 (not_5_out, Data[5]);
  not not_6 (not_6_out, Data[7]);
  and and_3 (and_3_out, Data[0], Data[1], not_2_out, not_3_out, not_4_out, not_5_out, Data[6], not_6_out, not_7_out, not_8_out, not_9_out, not_10_out, not_11_out, not_12_out, not_13_out, not_14_out);
  not not_7 (not_7_out, Data[8]);
  not not_8 (not_8_out, Data[9]);
  not not_9 (not_9_out, Data[10]);
  not not_10 (not_10_out, Data[11]);
  not not_11 (not_11_out, Data[12]);
  not not_12 (not_12_out, Data[13]);
  not not_13 (not_13_out, Data[14]);
  not not_14 (not_14_out, Data[15]);
  not not_15 (not_15_out, Data[0]);
  not not_16 (not_16_out, Data[2]);
  not not_17 (not_17_out, Data[3]);
  not not_18 (not_18_out, Data[4]);
  not not_19 (not_19_out, Data[5]);
  not not_20 (not_20_out, Data[7]);
  and and_4 (and_4_out, not_15_out, Data[1], not_16_out, not_17_out, not_18_out, not_19_out, Data[6], not_20_out, not_21_out, not_22_out, not_23_out, not_24_out, not_25_out, not_26_out, not_27_out, not_28_out);
  not not_21 (not_21_out, Data[8]);
  not not_22 (not_22_out, Data[9]);
  not not_23 (not_23_out, Data[10]);
  not not_24 (not_24_out, Data[11]);
  not not_25 (not_25_out, Data[12]);
  not not_26 (not_26_out, Data[13]);
  not not_27 (not_27_out, Data[14]);
  not not_28 (not_28_out, Data[15]);
  not not_29 (not_29_out, Data[1]);
  not not_30 (not_30_out, Data[2]);
  not not_31 (not_31_out, Data[3]);
  not not_32 (not_32_out, Data[4]);
  not not_33 (not_33_out, Data[5]);
  not not_34 (not_34_out, Data[7]);
  and and_5 (and_5_out, Data[0], not_29_out, not_30_out, not_31_out, not_32_out, not_33_out, Data[6], not_34_out, not_35_out, not_36_out, not_37_out, not_38_out, not_39_out, not_40_out, not_41_out, not_42_out);
  not not_35 (not_35_out, Data[8]);
  not not_36 (not_36_out, Data[9]);
  not not_37 (not_37_out, Data[10]);
  not not_38 (not_38_out, Data[11]);
  not not_39 (not_39_out, Data[12]);
  not not_40 (not_40_out, Data[13]);
  not not_41 (not_41_out, Data[14]);
  not not_42 (not_42_out, Data[15]);
  not not_43 (not_43_out, Data[0]);
  not not_44 (not_44_out, Data[1]);
  not not_45 (not_45_out, Data[2]);
  not not_46 (not_46_out, Data[3]);
  not not_47 (not_47_out, Data[4]);
  not not_48 (not_48_out, Data[5]);
  not not_49 (not_49_out, Data[7]);
  and and_6 (and_6_out, not_43_out, not_44_out, not_45_out, not_46_out, not_47_out, not_48_out, Data[6], not_49_out, not_50_out, not_51_out, not_52_out, not_53_out, not_54_out, not_55_out, not_56_out, not_57_out);
  not not_50 (not_50_out, Data[8]);
  not not_51 (not_51_out, Data[9]);
  not not_52 (not_52_out, Data[10]);
  not not_53 (not_53_out, Data[11]);
  not not_54 (not_54_out, Data[12]);
  not not_55 (not_55_out, Data[13]);
  not not_56 (not_56_out, Data[14]);
  not not_57 (not_57_out, Data[15]);
  not not_58 (not_58_out, Data[2]);
  not not_59 (not_59_out, Data[3]);
  not not_60 (not_60_out, Data[6]);
  not not_61 (not_61_out, Data[7]);
  and and_7 (and_7_out, Data[0], Data[1], not_58_out, not_59_out, Data[4], Data[5], not_60_out, not_61_out, not_62_out, not_63_out, not_64_out, not_65_out, not_66_out, not_67_out, not_68_out, not_69_out);
  not not_62 (not_62_out, Data[8]);
  not not_63 (not_63_out, Data[9]);
  not not_64 (not_64_out, Data[10]);
  not not_65 (not_65_out, Data[11]);
  not not_66 (not_66_out, Data[12]);
  not not_67 (not_67_out, Data[13]);
  not not_68 (not_68_out, Data[14]);
  not not_69 (not_69_out, Data[15]);
  not not_70 (not_70_out, Data[0]);
  not not_71 (not_71_out, Data[2]);
  not not_72 (not_72_out, Data[3]);
  not not_73 (not_73_out, Data[6]);
  not not_74 (not_74_out, Data[7]);
  and and_8 (and_8_out, not_70_out, Data[1], not_71_out, not_72_out, Data[4], Data[5], not_73_out, not_74_out, not_75_out, not_76_out, not_77_out, not_78_out, not_79_out, not_80_out, not_81_out, not_82_out);
  not not_75 (not_75_out, Data[8]);
  not not_76 (not_76_out, Data[9]);
  not not_77 (not_77_out, Data[10]);
  not not_78 (not_78_out, Data[11]);
  not not_79 (not_79_out, Data[12]);
  not not_80 (not_80_out, Data[13]);
  not not_81 (not_81_out, Data[14]);
  not not_82 (not_82_out, Data[15]);
  not not_83 (not_83_out, Data[1]);
  not not_84 (not_84_out, Data[2]);
  not not_85 (not_85_out, Data[3]);
  not not_86 (not_86_out, Data[6]);
  not not_87 (not_87_out, Data[7]);
  and and_9 (and_9_out, Data[0], not_83_out, not_84_out, not_85_out, Data[4], Data[5], not_86_out, not_87_out, not_88_out, not_89_out, not_90_out, not_91_out, not_92_out, not_93_out, not_94_out, not_95_out);
  not not_88 (not_88_out, Data[8]);
  not not_89 (not_89_out, Data[9]);
  not not_90 (not_90_out, Data[10]);
  not not_91 (not_91_out, Data[11]);
  not not_92 (not_92_out, Data[12]);
  not not_93 (not_93_out, Data[13]);
  not not_94 (not_94_out, Data[14]);
  not not_95 (not_95_out, Data[15]);
  not not_96 (not_96_out, Data[0]);
  not not_97 (not_97_out, Data[1]);
  not not_98 (not_98_out, Data[2]);
  not not_99 (not_99_out, Data[3]);
  not not_100 (not_100_out, Data[6]);
  not not_101 (not_101_out, Data[7]);
  and and_10 (and_10_out, not_96_out, not_97_out, not_98_out, not_99_out, Data[4], Data[5], not_100_out, not_101_out, not_102_out, not_103_out, not_104_out, not_105_out, not_106_out, not_107_out, not_108_out, not_109_out);
  not not_102 (not_102_out, Data[8]);
  not not_103 (not_103_out, Data[9]);
  not not_104 (not_104_out, Data[10]);
  not not_105 (not_105_out, Data[11]);
  not not_106 (not_106_out, Data[12]);
  not not_107 (not_107_out, Data[13]);
  not not_108 (not_108_out, Data[14]);
  not not_109 (not_109_out, Data[15]);
  not not_110 (not_110_out, Data[1]);
  not not_111 (not_111_out, Data[2]);
  not not_112 (not_112_out, Data[3]);
  not not_113 (not_113_out, Data[4]);
  not not_114 (not_114_out, Data[6]);
  not not_115 (not_115_out, Data[7]);
  and and_11 (and_11_out, Data[0], not_110_out, not_111_out, not_112_out, not_113_out, Data[5], not_114_out, not_115_out, not_116_out, not_117_out, not_118_out, not_119_out, not_120_out, not_121_out, not_122_out, not_123_out);
  not not_116 (not_116_out, Data[8]);
  not not_117 (not_117_out, Data[9]);
  not not_118 (not_118_out, Data[10]);
  not not_119 (not_119_out, Data[11]);
  not not_120 (not_120_out, Data[12]);
  not not_121 (not_121_out, Data[13]);
  not not_122 (not_122_out, Data[14]);
  not not_123 (not_123_out, Data[15]);
  not not_124 (not_124_out, Data[0]);
  not not_125 (not_125_out, Data[1]);
  not not_126 (not_126_out, Data[2]);
  not not_127 (not_127_out, Data[3]);
  not not_128 (not_128_out, Data[4]);
  not not_129 (not_129_out, Data[6]);
  not not_130 (not_130_out, Data[7]);
  and and_12 (and_12_out, not_124_out, not_125_out, not_126_out, not_127_out, not_128_out, Data[5], not_129_out, not_130_out, not_131_out, not_132_out, not_133_out, not_134_out, not_135_out, not_136_out, not_137_out, not_138_out);
  not not_131 (not_131_out, Data[8]);
  not not_132 (not_132_out, Data[9]);
  not not_133 (not_133_out, Data[10]);
  not not_134 (not_134_out, Data[11]);
  not not_135 (not_135_out, Data[12]);
  not not_136 (not_136_out, Data[13]);
  not not_137 (not_137_out, Data[14]);
  not not_138 (not_138_out, Data[15]);
  not not_139 (not_139_out, Data[1]);
  not not_140 (not_140_out, Data[3]);
  not not_141 (not_141_out, Data[5]);
  not not_142 (not_142_out, Data[6]);
  not not_143 (not_143_out, Data[7]);
  and and_13 (and_13_out, Data[0], not_139_out, Data[2], not_140_out, Data[4], not_141_out, not_142_out, not_143_out, not_144_out, not_145_out, not_146_out, not_147_out, not_148_out, not_149_out, not_150_out, not_151_out);
  not not_144 (not_144_out, Data[8]);
  not not_145 (not_145_out, Data[9]);
  not not_146 (not_146_out, Data[10]);
  not not_147 (not_147_out, Data[11]);
  not not_148 (not_148_out, Data[12]);
  not not_149 (not_149_out, Data[13]);
  not not_150 (not_150_out, Data[14]);
  not not_151 (not_151_out, Data[15]);
  not not_152 (not_152_out, Data[0]);
  not not_153 (not_153_out, Data[1]);
  not not_154 (not_154_out, Data[3]);
  not not_155 (not_155_out, Data[5]);
  not not_156 (not_156_out, Data[6]);
  not not_157 (not_157_out, Data[7]);
  and and_14 (and_14_out, not_152_out, not_153_out, Data[2], not_154_out, Data[4], not_155_out, not_156_out, not_157_out, not_158_out, not_159_out, not_160_out, not_161_out, not_162_out, not_163_out, not_164_out, not_165_out);
  not not_158 (not_158_out, Data[8]);
  not not_159 (not_159_out, Data[9]);
  not not_160 (not_160_out, Data[10]);
  not not_161 (not_161_out, Data[11]);
  not not_162 (not_162_out, Data[12]);
  not not_163 (not_163_out, Data[13]);
  not not_164 (not_164_out, Data[14]);
  not not_165 (not_165_out, Data[15]);
  not not_166 (not_166_out, Data[2]);
  not not_167 (not_167_out, Data[3]);
  not not_168 (not_168_out, Data[5]);
  not not_169 (not_169_out, Data[6]);
  not not_170 (not_170_out, Data[7]);
  and and_15 (and_15_out, Data[0], Data[1], not_166_out, not_167_out, Data[4], not_168_out, not_169_out, not_170_out, not_171_out, not_172_out, not_173_out, not_174_out, not_175_out, not_176_out, not_177_out, not_178_out);
  not not_171 (not_171_out, Data[8]);
  not not_172 (not_172_out, Data[9]);
  not not_173 (not_173_out, Data[10]);
  not not_174 (not_174_out, Data[11]);
  not not_175 (not_175_out, Data[12]);
  not not_176 (not_176_out, Data[13]);
  not not_177 (not_177_out, Data[14]);
  not not_178 (not_178_out, Data[15]);
  not not_179 (not_179_out, Data[0]);
  not not_180 (not_180_out, Data[2]);
  not not_181 (not_181_out, Data[3]);
  not not_182 (not_182_out, Data[5]);
  not not_183 (not_183_out, Data[6]);
  not not_184 (not_184_out, Data[7]);
  and and_16 (and_16_out, not_179_out, Data[1], not_180_out, not_181_out, Data[4], not_182_out, not_183_out, not_184_out, not_185_out, not_186_out, not_187_out, not_188_out, not_189_out, not_190_out, not_191_out, not_192_out);
  not not_185 (not_185_out, Data[8]);
  not not_186 (not_186_out, Data[9]);
  not not_187 (not_187_out, Data[10]);
  not not_188 (not_188_out, Data[11]);
  not not_189 (not_189_out, Data[12]);
  not not_190 (not_190_out, Data[13]);
  not not_191 (not_191_out, Data[14]);
  not not_192 (not_192_out, Data[15]);
  not not_193 (not_193_out, Data[1]);
  not not_194 (not_194_out, Data[2]);
  not not_195 (not_195_out, Data[3]);
  not not_196 (not_196_out, Data[5]);
  not not_197 (not_197_out, Data[6]);
  not not_198 (not_198_out, Data[7]);
  and and_17 (and_17_out, Data[0], not_193_out, not_194_out, not_195_out, Data[4], not_196_out, not_197_out, not_198_out, not_199_out, not_200_out, not_201_out, not_202_out, not_203_out, not_204_out, not_205_out, not_206_out);
  not not_199 (not_199_out, Data[8]);
  not not_200 (not_200_out, Data[9]);
  not not_201 (not_201_out, Data[10]);
  not not_202 (not_202_out, Data[11]);
  not not_203 (not_203_out, Data[12]);
  not not_204 (not_204_out, Data[13]);
  not not_205 (not_205_out, Data[14]);
  not not_206 (not_206_out, Data[15]);
  not not_207 (not_207_out, Data[0]);
  not not_208 (not_208_out, Data[1]);
  not not_209 (not_209_out, Data[2]);
  not not_210 (not_210_out, Data[3]);
  not not_211 (not_211_out, Data[5]);
  not not_212 (not_212_out, Data[6]);
  not not_213 (not_213_out, Data[7]);
  and and_18 (and_18_out, not_207_out, not_208_out, not_209_out, not_210_out, Data[4], not_211_out, not_212_out, not_213_out, not_214_out, not_215_out, not_216_out, not_217_out, not_218_out, not_219_out, not_220_out, not_221_out);
  not not_214 (not_214_out, Data[8]);
  not not_215 (not_215_out, Data[9]);
  not not_216 (not_216_out, Data[10]);
  not not_217 (not_217_out, Data[11]);
  not not_218 (not_218_out, Data[12]);
  not not_219 (not_219_out, Data[13]);
  not not_220 (not_220_out, Data[14]);
  not not_221 (not_221_out, Data[15]);
  not not_222 (not_222_out, Data[0]);
  not not_223 (not_223_out, Data[2]);
  not not_224 (not_224_out, Data[3]);
  not not_225 (not_225_out, Data[4]);
  not not_226 (not_226_out, Data[5]);
  not not_227 (not_227_out, Data[6]);
  not not_228 (not_228_out, Data[7]);
  and and_19 (and_19_out, not_222_out, Data[1], not_223_out, not_224_out, not_225_out, not_226_out, not_227_out, not_228_out, not_229_out, not_230_out, not_231_out, not_232_out, not_233_out, not_234_out, not_235_out, not_236_out);
  not not_229 (not_229_out, Data[8]);
  not not_230 (not_230_out, Data[9]);
  not not_231 (not_231_out, Data[10]);
  not not_232 (not_232_out, Data[11]);
  not not_233 (not_233_out, Data[12]);
  not not_234 (not_234_out, Data[13]);
  not not_235 (not_235_out, Data[14]);
  not not_236 (not_236_out, Data[15]);
  not not_237 (not_237_out, Data[1]);
  not not_238 (not_238_out, Data[2]);
  not not_239 (not_239_out, Data[3]);
  not not_240 (not_240_out, Data[4]);
  not not_241 (not_241_out, Data[5]);
  not not_242 (not_242_out, Data[6]);
  not not_243 (not_243_out, Data[7]);
  and and_20 (and_20_out, Data[0], not_237_out, not_238_out, not_239_out, not_240_out, not_241_out, not_242_out, not_243_out, not_244_out, not_245_out, not_246_out, not_247_out, not_248_out, not_249_out, not_250_out, not_251_out);
  not not_244 (not_244_out, Data[8]);
  not not_245 (not_245_out, Data[9]);
  not not_246 (not_246_out, Data[10]);
  not not_247 (not_247_out, Data[11]);
  not not_248 (not_248_out, Data[12]);
  not not_249 (not_249_out, Data[13]);
  not not_250 (not_250_out, Data[14]);
  not not_251 (not_251_out, Data[15]);
  not not_252 (not_252_out, Data[0]);
  not not_253 (not_253_out, Data[1]);
  not not_254 (not_254_out, Data[2]);
  not not_255 (not_255_out, Data[3]);
  not not_256 (not_256_out, Data[4]);
  not not_257 (not_257_out, Data[5]);
  not not_258 (not_258_out, Data[6]);
  not not_259 (not_259_out, Data[7]);
  and and_21 (and_21_out, not_252_out, not_253_out, not_254_out, not_255_out, not_256_out, not_257_out, not_258_out, not_259_out, not_260_out, not_261_out, not_262_out, not_263_out, not_264_out, not_265_out, not_266_out, not_267_out);
  not not_260 (not_260_out, Data[8]);
  not not_261 (not_261_out, Data[9]);
  not not_262 (not_262_out, Data[10]);
  not not_263 (not_263_out, Data[11]);
  not not_264 (not_264_out, Data[12]);
  not not_265 (not_265_out, Data[13]);
  not not_266 (not_266_out, Data[14]);
  not not_267 (not_267_out, Data[15]);
  assign HALT = Enable ? and_1_out : 1'bz;  // Controlled_Buffer controlled_buffer_1
  assign NOOP = Enable ? and_2_out : 1'bz;  // Controlled_Buffer controlled_buffer_2
  assign SUB_R2R = Enable ? and_3_out : 1'bz;  // Controlled_Buffer controlled_buffer_3
  assign ADD_R2R = Enable ? and_4_out : 1'bz;  // Controlled_Buffer controlled_buffer_4
  assign SUB_R2V = Enable ? and_5_out : 1'bz;  // Controlled_Buffer controlled_buffer_5
  assign ADD_R2V = Enable ? and_6_out : 1'bz;  // Controlled_Buffer controlled_buffer_6
  assign JMP = Enable ? and_7_out : 1'bz;  // Controlled_Buffer controlled_buffer_7
  assign JLT = Enable ? and_8_out : 1'bz;  // Controlled_Buffer controlled_buffer_8
  assign JGT = Enable ? and_9_out : 1'bz;  // Controlled_Buffer controlled_buffer_9
  assign JEQ = Enable ? and_10_out : 1'bz;  // Controlled_Buffer controlled_buffer_10
  assign CMP_R2V = Enable ? and_11_out : 1'bz;  // Controlled_Buffer controlled_buffer_11
  assign CMP_R2R = Enable ? and_12_out : 1'bz;  // Controlled_Buffer controlled_buffer_12
  assign STH_R2R = Enable ? and_13_out : 1'bz;  // Controlled_Buffer controlled_buffer_13
  assign STL_R2R = Enable ? and_14_out : 1'bz;  // Controlled_Buffer controlled_buffer_14
  assign ST_R2R = Enable ? and_15_out : 1'bz;  // Controlled_Buffer controlled_buffer_15
  assign STH_R2V = Enable ? and_16_out : 1'bz;  // Controlled_Buffer controlled_buffer_16
  assign STL_R2M = Enable ? and_17_out : 1'bz;  // Controlled_Buffer controlled_buffer_17
  assign ST_R2M = Enable ? and_18_out : 1'bz;  // Controlled_Buffer controlled_buffer_18
  assign LD_R2M = Enable ? and_19_out : 1'bz;  // Controlled_Buffer controlled_buffer_19
  assign LD_R2R = Enable ? and_20_out : 1'bz;  // Controlled_Buffer controlled_buffer_20
  assign LD_R2V = Enable ? and_21_out : 1'bz;  // Controlled_Buffer controlled_buffer_21
endmodule

module RegisterFile (
  input  Clock,
  input  Reset,
  input  [15:0] Data,
  input  [7:0] Read_Addr,
  input  [7:0] Write_Addr,
  output [15:0] Out_Data
);

  wire decoder_4_1_o0, decoder_4_1_o1, decoder_4_1_o2, decoder_4_1_o3, decoder_4_1_o4, decoder_4_1_o5,
       decoder_4_1_o6, decoder_4_1_o7, decoder_4_2_o0, decoder_4_2_o1, decoder_4_2_o2, decoder_4_2_o3,
       decoder_4_2_o4, decoder_4_2_o5, decoder_4_2_o6, decoder_4_2_o7;
  wire [15:0] register_1_q, register_2_q, register_3_q, register_4_q, register_5_q, register_6_q,
       register_7_q, register_8_q;

  Register #(.width(16)) register_1 (.D(Data), .en(decoder_4_2_o0), .clk(Clock), .Q(register_1_q), .clr(Reset));
  Register #(.width(16)) register_2 (.D(Data), .en(decoder_4_2_o1), .clk(Clock), .Q(register_2_q), .clr(Reset));
  Register #(.width(16)) register_3 (.D(Data), .en(decoder_4_2_o2), .clk(Clock), .Q(register_3_q), .clr(Reset));
  Register #(.width(16)) register_4 (.D(Data), .en(decoder_4_2_o3), .clk(Clock), .Q(register_4_q), .clr(Reset));
  Register #(.width(16)) register_5 (.D(Data), .en(decoder_4_2_o4), .clk(Clock), .Q(register_5_q), .clr(Reset));
  Register #(.width(16)) register_6 (.D(Data), .en(decoder_4_2_o5), .clk(Clock), .Q(register_6_q), .clr(Reset));
  Register #(.width(16)) register_7 (.D(Data), .en(decoder_4_2_o6), .clk(Clock), .Q(register_7_q), .clr(Reset));
  Register #(.width(16)) register_8 (.D(Data), .en(decoder_4_2_o7), .clk(Clock), .Q(register_8_q), .clr(Reset));
  assign Out_Data = decoder_4_1_o0 ? register_1_q : 16'bz;  // Controlled_Buffer controlled_buffer_1
  assign Out_Data = decoder_4_1_o1 ? register_2_q : 16'bz;  // Controlled_Buffer controlled_buffer_2
  assign Out_Data = decoder_4_1_o2 ? register_3_q : 16'bz;  // Controlled_Buffer controlled_buffer_3
  assign Out_Data = decoder_4_1_o3 ? register_4_q : 16'bz;  // Controlled_Buffer controlled_buffer_4
  assign Out_Data = decoder_4_1_o4 ? register_5_q : 16'bz;  // Controlled_Buffer controlled_buffer_5
  assign Out_Data = decoder_4_1_o5 ? register_6_q : 16'bz;  // Controlled_Buffer controlled_buffer_6
  assign Out_Data = decoder_4_1_o6 ? register_7_q : 16'bz;  // Controlled_Buffer controlled_buffer_7
  assign Out_Data = decoder_4_1_o7 ? register_8_q : 16'bz;  // Controlled_Buffer controlled_buffer_8
  decoder_4 decoder_4_1 (
    .Input(Read_Addr[3:0]), .O0(decoder_4_1_o0), .O1(decoder_4_1_o1), .O2(decoder_4_1_o2),
    .O3(decoder_4_1_o3), .O4(decoder_4_1_o4), .O5(decoder_4_1_o5), .O6(decoder_4_1_o6), .O7(decoder_4_1_o7));  // open: O8, O9, O10, O11, O12, O13, O14, O15
  decoder_4 decoder_4_2 (
    .Input(Write_Addr[3:0]), .O0(decoder_4_2_o0), .O1(decoder_4_2_o1), .O2(decoder_4_2_o2),
    .O3(decoder_4_2_o3), .O4(decoder_4_2_o4), .O5(decoder_4_2_o5), .O6(decoder_4_2_o6), .O7(decoder_4_2_o7));  // open: O8, O9, O10, O11, O12, O13, O14, O15
endmodule

module decoder_4 (
  input  [3:0] Input,
  output O0,
  output O1,
  output O2,
  output O3,
  output O4,
  output O5,
  output O6,
  output O7,
  output O8,
  output O9,
  output O10,
  output O11,
  output O12,
  output O13,
  output O14,
  output O15
);

  wire not_1_out, not_2_out, not_3_out, not_4_out;

  not not_1 (not_1_out, Input[3]);
  not not_2 (not_2_out, Input[2]);
  not not_3 (not_3_out, Input[1]);
  not not_4 (not_4_out, Input[0]);
  and and_1 (O0, not_1_out, not_2_out, not_3_out, not_4_out);
  and and_2 (O1, not_1_out, not_2_out, not_3_out, Input[0]);
  and and_3 (O2, not_1_out, not_2_out, Input[1], not_4_out);
  and and_4 (O3, not_1_out, not_2_out, Input[1], Input[0]);
  and and_5 (O4, not_1_out, Input[2], not_3_out, not_4_out);
  and and_6 (O5, not_1_out, Input[2], not_3_out, Input[0]);
  and and_7 (O6, not_1_out, Input[2], Input[1], not_4_out);
  and and_8 (O7, not_1_out, Input[2], Input[1], Input[0]);
  and and_9 (O8, Input[3], not_2_out, not_3_out, not_4_out);
  and and_10 (O9, Input[3], not_2_out, not_3_out, Input[0]);
  and and_11 (O10, Input[3], not_2_out, Input[1], not_4_out);
  and and_12 (O11, Input[3], not_2_out, Input[1], Input[0]);
  and and_13 (O12, Input[3], Input[2], not_3_out, not_4_out);
  and and_14 (O13, Input[3], Input[2], not_3_out, Input[0]);
  and and_15 (O14, Input[3], Input[2], Input[1], not_4_out);
  and and_16 (O15, Input[3], Input[2], Input[1], Input[0]);
endmodule
